// Logisim project parte1_memoria.circ as structural Verilog
module main (
  input  A5,
  input  A4,
  input  A3,
  input  A2,
  input  A1,
  input  A0
);

  _74139 #(.ShowInternalStructure("true")) Decodificador (
    .pin2(A5), .pin3(A4));  // open: pin1, pin4, pin5, pin6, pin7, pin15, pin14, pin13, pin12, pin11, pin10, pin9
  RAM #(.addrWidth(6), .\type ("nonvolatile")) ram_1 ();  // open: addr, we, oe, clk, din, dout
  ROM #(.addrWidth(6)) rom_1 ();  // open: addr, data
  Register BancoDeRegistradores ();  // open: D, en, clk, Q, clr

  // Notes on the sheet:
  //   6 bits de endereçamento ( A5 . . . A0)
endmodule
