// Logisim project parte1_memoria.circ as structural Verilog
module main (
  input  A5,
  input  A4,
  input  A3,
  input  A2,
  input  A1,
  input  A0
);

  wire Decodificador_pin1, Decodificador_pin4, Decodificador_pin5, Decodificador_pin6, Decodificador_pin7,
       not_1_out, not_2_out, not_3_out, not_4_out;
  wire [7:0] multiplexer_1_out, ram_1_dout, ram_2_dout, ram_3_dout, rom_1_data;

  _74139 #(.ShowInternalStructure("true")) Decodificador (
    .pin1(Decodificador_pin1), .pin2(A4), .pin3(A5), .pin4(Decodificador_pin4), .pin5(Decodificador_pin5),
    .pin6(Decodificador_pin6), .pin7(Decodificador_pin7));  // open: pin15, pin14, pin13, pin12, pin11, pin10, pin9
  not not_1 (not_1_out, Decodificador_pin4);
  not not_2 (not_2_out, Decodificador_pin5);
  not not_3 (not_3_out, Decodificador_pin6);
  LED CS_RAM (.in(not_2_out));
  LED CS_ROM (.in(not_1_out));
  LED CS_REG (.in(not_3_out));
  not not_4 (not_4_out, Decodificador_pin7);
  LED CS_IO (.in(not_4_out));
  ROM #(.addrWidth(4)) rom_1 (.addr({A3, A2, A1, A0}), .data(rom_1_data));
  RAM #(.addrWidth(4), .\type ("nonvolatile")) ram_1 (
    .addr({A3, A2, A1, A0}), .oe(not_2_out), .dout(ram_1_dout));  // open: we, clk, din
  RAM #(.addrWidth(4), .trigger("falling")) ram_2 (
    .addr({A3, A2, A1, A0}), .oe(not_3_out), .dout(ram_2_dout));  // open: we, clk, din
  RAM #(.addrWidth(4)) ram_3 (.addr({A3, A2, A1, A0}), .oe(not_4_out), .dout(ram_3_dout));  // open: we, clk, din
  Multiplexer #(.select(2), .width(8)) multiplexer_1 (
    .in0(rom_1_data), .in1(ram_1_dout), .in2(ram_2_dout), .in3(ram_3_dout), .out(multiplexer_1_out),
    .sel({A5, A4}));
  // also tied to GND on the sheet: Decodificador_pin1

  // Notes on the sheet:
  //   6 bits de endereçamento ( A5 . . . A0)
  //   Banco de registradores
  //   E/S
  //   se conecta a cache
endmodule
