// Logisim project maquinaDeEstadosUC.circ as structural Verilog: 1 circuit, main circuit main
module main (
  input  OP,
  input  Reset,
  output MemRead,
  output PcWrite,
  output IRWrite,
  output ALUSrcB0,
  output PcSource,
  output ALUOp1,
  output ALUOp0
);

  wire and_1_out, and_3_out, and_4_out, and_5_out, and_6_out, clock_1_out, d_ff_1_qn, d_ff_2_qn, d_ff_3_qn,
       not_1_out, or_1_out;
  wire [0:0] bcd_to_7_segment_decoder_1_p1;

  Clock clock_1 (.out(clock_1_out));
  not not_1 (not_1_out, OP);
  // BCD_to_7_Segment_decoder bcd_to_7_segment_decoder_1: pin names not known; wires that end beside it: {1'b0, ALUOp0, ALUOp1, bcd_to_7_segment_decoder_1_p1[0]}
  _7_Segment_Display u_7_segment_display_1 ();  // open: g, f, a, b, e, d, c, dp
  D_Flip_Flop d_ff_1 (.D(and_3_out), .clk(clock_1_out), .Q(ALUOp0), .Qn(d_ff_1_qn), .reset(Reset));  // open: preset
  D_Flip_Flop d_ff_2 (.D(or_1_out), .clk(clock_1_out), .Q(ALUOp1), .Qn(d_ff_2_qn), .reset(Reset));  // open: preset
  D_Flip_Flop d_ff_3 (
    .D(and_1_out), .clk(clock_1_out), .Q(bcd_to_7_segment_decoder_1_p1[0]), .Qn(d_ff_3_qn), .reset(Reset));  // open: preset
  and and_1 (and_1_out, d_ff_1_qn, d_ff_3_qn);
  and and_2 (ALUSrcB0, ~bcd_to_7_segment_decoder_1_p1[0], ~ALUOp1, ~ALUOp0);  // AND_Gate
  and and_3 (and_3_out, not_1_out, and_6_out);
  and and_4 (and_4_out, ALUOp1, d_ff_3_qn);
  and and_5 (and_5_out, OP, and_6_out);
  and and_6 (and_6_out, d_ff_1_qn, d_ff_2_qn, bcd_to_7_segment_decoder_1_p1[0]);
  or or_1 (or_1_out, and_4_out, and_5_out);

  assign IRWrite = ALUSrcB0;
  assign MemRead = ALUSrcB0;
  assign PcSource = ALUOp0;
  assign PcWrite = ALUSrcB0;

  // Notes on the sheet:
  //   estado atual
  //   Q2
  //   Q1
  //   Q0
  //   LogicaD2
  //   LogicaD0
  //   logicaD1
  //   Sinal de estado S1
  //   a máquina está em S1(001)
endmodule
